// Logisim project Flip-Flop-D.circ as structural Verilog: 1 circuit, main circuit main
module main (
  input  DATA_IN,
  output Q,
  output nQ
);

  wire not_1_out;

  not not_1 (not_1_out, DATA_IN);
  nor nor_1 (Q, DATA_IN, nQ);
  nor nor_2 (nQ, Q, not_1_out);

  // Notes on the sheet:
  //   Flip-Flop tipo D (LATCH)
endmodule
